// Logisim project CPU_Design.circ as structural Verilog: 7 circuits, main circuit main
module main (
);

  wire and_1_out, Clk_out, control_unit_1_b_select, control_unit_1_c_select, control_unit_1_ir_enable,
       control_unit_1_ma_select, control_unit_1_move_select, control_unit_1_pc_enable,
       control_unit_1_read_enable, control_unit_1_rf_write, control_unit_1_write_enable,
       control_unit_1_y_select, control_unit_1_z_select, d_ff_1_q, ir_pc_mem_block_1_hlt;
  wire [1:0] control_unit_1_alu_select;
  wire [4:0] ir_pc_mem_block_1_ir_21_17, ir_pc_mem_block_1_ir_26_22, ir_pc_mem_block_1_ir_31_27,
       multiplexer_1_out;
  wire [5:0] ir_pc_mem_block_1_op;
  wire [15:0] ir_pc_mem_block_1_immediate;
  wire [31:0] alu_1_ouput, bit_extender_32_1_output_32_bit, ir_pc_mem_block_1_data_out, multiplexer_2_out,
       multiplexer_3_out, multiplexer_4_out, multiplexer_5_out, Ra_q, Rb_q, register_file_1_a,
       register_file_1_b, Rm_q, Ry_q, Rz_q;

  Clock Clk (.out(Clk_out));
  D_Flip_Flop d_ff_1 (.Q(d_ff_1_q), .reset(ir_pc_mem_block_1_hlt));  // open: D, clk, Qn, preset
  and and_1 (and_1_out, Clk_out, d_ff_1_q);
  Multiplexer #(.width(5)) multiplexer_1 (
    .in0(ir_pc_mem_block_1_ir_21_17), .in1(ir_pc_mem_block_1_ir_26_22), .out(multiplexer_1_out),
    .sel(control_unit_1_c_select));
  Register_File register_file_1 (
    .C(Ry_q), .RF_write(control_unit_1_rf_write), .Clock(and_1_out), .Address_C(multiplexer_1_out),
    .Address_A(ir_pc_mem_block_1_ir_31_27), .Address_B(ir_pc_mem_block_1_ir_26_22), .A(register_file_1_a),
    .B(register_file_1_b));
  Register #(.width(32)) Ra (.D(register_file_1_a), .en(1'b1), .clk(and_1_out), .Q(Ra_q));  // open: clr
  Register #(.width(32)) Rb (.D(register_file_1_b), .en(1'b1), .clk(and_1_out), .Q(Rb_q));  // open: clr
  Multiplexer #(.width(32)) multiplexer_2 (
    .in0(Rb_q), .in1(bit_extender_32_1_output_32_bit), .out(multiplexer_2_out), .sel(control_unit_1_b_select));
  Multiplexer #(.width(32)) multiplexer_3 (
    .in0(Ra_q), .in1(multiplexer_2_out), .out(multiplexer_3_out), .sel(control_unit_1_move_select));
  ALU alu_1 (.InA(Ra_q), .InB(multiplexer_2_out), .ALU_sel(control_unit_1_alu_select), .Ouput(alu_1_ouput));
  Bit_extender_32 bit_extender_32_1 (
    .Input_16_bit(ir_pc_mem_block_1_immediate), .Output_32_bit(bit_extender_32_1_output_32_bit));
  IR_PC_Mem_Block ir_pc_mem_block_1 (
    .IR_enable(control_unit_1_ir_enable), .Rz(Rz_q), .MA_select(control_unit_1_ma_select),
    .PC_enable(control_unit_1_pc_enable), .write_enable(control_unit_1_write_enable),
    .read_enable(control_unit_1_read_enable), .data_in(Rm_q), .Clock(and_1_out), .OP(ir_pc_mem_block_1_op),
    .Immediate(ir_pc_mem_block_1_immediate), .IR_21_17(ir_pc_mem_block_1_ir_21_17),
    .IR_26_22(ir_pc_mem_block_1_ir_26_22), .IR_31_27(ir_pc_mem_block_1_ir_31_27),
    .data_out(ir_pc_mem_block_1_data_out), .hlt(ir_pc_mem_block_1_hlt));
  Control_Unit control_unit_1 (
    .OP(ir_pc_mem_block_1_op), .Clock(and_1_out), .RF_write(control_unit_1_rf_write),
    .C_select(control_unit_1_c_select), .B_select(control_unit_1_b_select),
    .ALU_select(control_unit_1_alu_select), .move_select(control_unit_1_move_select),
    .Z_select(control_unit_1_z_select), .Y_select(control_unit_1_y_select),
    .IR_enable(control_unit_1_ir_enable), .PC_enable(control_unit_1_pc_enable),
    .MA_select(control_unit_1_ma_select), .read_enable(control_unit_1_read_enable),
    .write_enable(control_unit_1_write_enable));
  Multiplexer #(.width(32)) multiplexer_4 (
    .in0(multiplexer_3_out), .in1(alu_1_ouput), .out(multiplexer_4_out), .sel(control_unit_1_z_select));
  Register #(.width(32)) Rz (.D(multiplexer_4_out), .en(1'b1), .clk(and_1_out), .Q(Rz_q));  // open: clr
  Register #(.width(32)) Rm (.D(Rb_q), .en(1'b1), .clk(and_1_out), .Q(Rm_q));  // open: clr
  Multiplexer #(.width(32)) multiplexer_5 (
    .in0(Rz_q), .in1(ir_pc_mem_block_1_data_out), .out(multiplexer_5_out), .sel(control_unit_1_y_select));
  Register #(.trigger("falling"), .width(32)) Ry (
    .D(multiplexer_5_out), .en(1'b1), .clk(and_1_out), .Q(Ry_q));  // open: clr
endmodule

module ALU (
  input  [31:0] InA,
  input  [31:0] InB,
  input  [1:0] ALU_sel,
  output [31:0] Ouput
);

  wire [31:0] adder_1_out, and_1_out, or_1_out, subtractor_1_out;

  Adder #(.width(32)) adder_1 (.a(InA), .b(InB), .out(adder_1_out));  // open: cin, cout
  Subtractor #(.width(32)) subtractor_1 (.a(InA), .b(InB), .out(subtractor_1_out));  // open: bin, bout
  assign and_1_out = InA & InB;  // AND_Gate and_1, 32 bits wide
  assign or_1_out = InA | InB;  // OR_Gate or_1, 32 bits wide
  Multiplexer #(.select(2), .width(32)) multiplexer_1 (
    .in0(adder_1_out), .in1(subtractor_1_out), .in2(and_1_out), .in3(or_1_out), .out(Ouput), .sel(ALU_sel));
endmodule

module Register_File (
  input  [31:0] C,
  input  RF_write,
  input  Clock,
  input  [4:0] Address_C,
  input  [4:0] Address_A,
  input  [4:0] Address_B,
  output [31:0] A,
  output [31:0] B
);

  wire decoder_1_out0, decoder_1_out1, decoder_1_out2, decoder_1_out3;
  wire [31:0] Register_10_out_r0, Register_10_out_r1, Register_10_out_r2, Register_10_out_r3,
       Register_10_out_r4, Register_10_out_r5, Register_10_out_r6, Register_10_out_r7, Register_11_out_r0,
       Register_11_out_r1, Register_11_out_r2, Register_11_out_r3, Register_11_out_r4, Register_11_out_r5,
       Register_11_out_r6, Register_11_out_r7, Register_Block_00_out_r0, Register_Block_00_out_r1,
       Register_Block_00_out_r2, Register_Block_00_out_r3, Register_Block_00_out_r4,
       Register_Block_00_out_r5, Register_Block_00_out_r6, Register_Block_00_out_r7,
       Register_Block_01_out_r0, Register_Block_01_out_r1, Register_Block_01_out_r2,
       Register_Block_01_out_r3, Register_Block_01_out_r4, Register_Block_01_out_r5,
       Register_Block_01_out_r6, Register_Block_01_out_r7;

  Decoder #(.select(2)) decoder_1 (
    .out0(decoder_1_out0), .out1(decoder_1_out1), .out2(decoder_1_out2), .out3(decoder_1_out3),
    .sel(Address_C[4:3]), .en(RF_write));
  Register_Block_8 Register_Block_00 (
    .C(C), .Sel_Reg_Blk(decoder_1_out0), .Address_Cx(Address_C[2:0]), .Clock(Clock),
    .Out_R0(Register_Block_00_out_r0), .Out_R1(Register_Block_00_out_r1), .Out_R2(Register_Block_00_out_r2),
    .Out_R3(Register_Block_00_out_r3), .Out_R4(Register_Block_00_out_r4), .Out_R5(Register_Block_00_out_r5),
    .Out_R6(Register_Block_00_out_r6), .Out_R7(Register_Block_00_out_r7));
  Register_Block_8 Register_Block_01 (
    .C(C), .Sel_Reg_Blk(decoder_1_out1), .Address_Cx(Address_C[2:0]), .Clock(Clock),
    .Out_R0(Register_Block_01_out_r0), .Out_R1(Register_Block_01_out_r1), .Out_R2(Register_Block_01_out_r2),
    .Out_R3(Register_Block_01_out_r3), .Out_R4(Register_Block_01_out_r4), .Out_R5(Register_Block_01_out_r5),
    .Out_R6(Register_Block_01_out_r6), .Out_R7(Register_Block_01_out_r7));
  Register_Block_8 Register_10 (
    .C(C), .Sel_Reg_Blk(decoder_1_out2), .Address_Cx(Address_C[2:0]), .Clock(Clock),
    .Out_R0(Register_10_out_r0), .Out_R1(Register_10_out_r1), .Out_R2(Register_10_out_r2),
    .Out_R3(Register_10_out_r3), .Out_R4(Register_10_out_r4), .Out_R5(Register_10_out_r5),
    .Out_R6(Register_10_out_r6), .Out_R7(Register_10_out_r7));
  Register_Block_8 Register_11 (
    .C(C), .Sel_Reg_Blk(decoder_1_out3), .Address_Cx(Address_C[2:0]), .Clock(Clock),
    .Out_R0(Register_11_out_r0), .Out_R1(Register_11_out_r1), .Out_R2(Register_11_out_r2),
    .Out_R3(Register_11_out_r3), .Out_R4(Register_11_out_r4), .Out_R5(Register_11_out_r5),
    .Out_R6(Register_11_out_r6), .Out_R7(Register_11_out_r7));
  Multiplexer #(.select(5), .width(32)) multiplexer_1 (
    .in0(Register_Block_00_out_r0), .in1(Register_Block_00_out_r1), .in2(Register_Block_00_out_r2),
    .in3(Register_Block_00_out_r3), .in4(Register_Block_00_out_r4), .in5(Register_Block_00_out_r5),
    .in6(Register_Block_00_out_r6), .in7(Register_Block_00_out_r7), .in8(Register_Block_01_out_r0),
    .in9(Register_Block_01_out_r1), .in10(Register_Block_01_out_r2), .in11(Register_Block_01_out_r3),
    .in12(Register_Block_01_out_r4), .in13(Register_Block_01_out_r5), .in14(Register_Block_01_out_r6),
    .in15(Register_Block_01_out_r7), .in16(Register_10_out_r0), .in17(Register_10_out_r1),
    .in18(Register_10_out_r2), .in19(Register_10_out_r3), .in20(Register_10_out_r4),
    .in21(Register_10_out_r5), .in22(Register_10_out_r6), .in23(Register_10_out_r7),
    .in24(Register_11_out_r0), .in25(Register_11_out_r1), .in26(Register_11_out_r2),
    .in27(Register_11_out_r3), .in28(Register_11_out_r4), .in29(Register_11_out_r5),
    .in30(Register_11_out_r6), .in31(Register_11_out_r7), .out(A), .sel(Address_A));
  Multiplexer #(.select(5), .width(32)) multiplexer_2 (
    .in0(Register_Block_00_out_r0), .in1(Register_Block_00_out_r1), .in2(Register_Block_00_out_r2),
    .in3(Register_Block_00_out_r3), .in4(Register_Block_00_out_r4), .in5(Register_Block_00_out_r5),
    .in6(Register_Block_00_out_r6), .in7(Register_Block_00_out_r7), .in8(Register_Block_01_out_r0),
    .in9(Register_Block_01_out_r1), .in10(Register_Block_01_out_r2), .in11(Register_Block_01_out_r3),
    .in12(Register_Block_01_out_r4), .in13(Register_Block_01_out_r5), .in14(Register_Block_01_out_r6),
    .in15(Register_Block_01_out_r7), .in16(Register_10_out_r0), .in17(Register_10_out_r1),
    .in18(Register_10_out_r2), .in19(Register_10_out_r3), .in20(Register_10_out_r4),
    .in21(Register_10_out_r5), .in22(Register_10_out_r6), .in23(Register_10_out_r7),
    .in24(Register_11_out_r0), .in25(Register_11_out_r1), .in26(Register_11_out_r2),
    .in27(Register_11_out_r3), .in28(Register_11_out_r4), .in29(Register_11_out_r5),
    .in30(Register_11_out_r6), .in31(Register_11_out_r7), .out(B), .sel(Address_B));
endmodule

module Register_Block_8 (
  input  [31:0] C,
  input  Sel_Reg_Blk,
  input  [2:0] Address_Cx,
  input  Clock,
  output [31:0] Out_R0,
  output [31:0] Out_R1,
  output [31:0] Out_R2,
  output [31:0] Out_R3,
  output [31:0] Out_R4,
  output [31:0] Out_R5,
  output [31:0] Out_R6,
  output [31:0] Out_R7
);

  wire decoder_1_out0, decoder_1_out1, decoder_1_out2, decoder_1_out3, decoder_1_out4, decoder_1_out5,
       decoder_1_out6, decoder_1_out7;

  Decoder #(.select(3)) decoder_1 (
    .out0(decoder_1_out0), .out1(decoder_1_out1), .out2(decoder_1_out2), .out3(decoder_1_out3),
    .out4(decoder_1_out4), .out5(decoder_1_out5), .out6(decoder_1_out6), .out7(decoder_1_out7),
    .sel(Address_Cx), .en(Sel_Reg_Blk));
  Register #(.width(32)) R0 (.D(C), .en(decoder_1_out0), .clk(Clock), .Q(Out_R0));  // open: clr
  Register #(.width(32)) R1 (.D(C), .en(decoder_1_out1), .clk(Clock), .Q(Out_R1));  // open: clr
  Register #(.width(32)) R2 (.D(C), .en(decoder_1_out2), .clk(Clock), .Q(Out_R2));  // open: clr
  Register #(.width(32)) R3 (.D(C), .en(decoder_1_out3), .clk(Clock), .Q(Out_R3));  // open: clr
  Register #(.width(32)) R4 (.D(C), .en(decoder_1_out4), .clk(Clock), .Q(Out_R4));  // open: clr
  Register #(.width(32)) R5 (.D(C), .en(decoder_1_out5), .clk(Clock), .Q(Out_R5));  // open: clr
  Register #(.width(32)) R6 (.D(C), .en(decoder_1_out6), .clk(Clock), .Q(Out_R6));  // open: clr
  Register #(.width(32)) R7 (.D(C), .en(decoder_1_out7), .clk(Clock), .Q(Out_R7));  // open: clr
endmodule

module Bit_extender_32 (
  input  [15:0] Input_16_bit,
  output [31:0] Output_32_bit
);


  assign Output_32_bit = {{16{1'b0}}, Input_16_bit};
endmodule

module IR_PC_Mem_Block (
  input  IR_enable,
  input  [31:0] Rz,
  input  MA_select,
  input  PC_enable,
  input  write_enable,
  input  read_enable,
  input  [31:0] data_in,
  input  Clock,
  output [5:0] OP,
  output [15:0] Immediate,
  output [4:0] IR_21_17,
  output [4:0] IR_26_22,
  output [4:0] IR_31_27,
  output [31:0] data_out,
  output hlt
);

  wire [31:0] adder_1_out, multiplexer_1_out, register_1_q;

  Register #(.width(32)) register_1 (.D(adder_1_out), .en(PC_enable), .clk(Clock), .Q(register_1_q), .clr(hlt));
  Adder #(.width(32)) adder_1 (.a(register_1_q), .b(32'h1), .out(adder_1_out));  // open: cin, cout
  Multiplexer #(.width(32)) multiplexer_1 (.in0(Rz), .in1(register_1_q), .out(multiplexer_1_out), .sel(MA_select));
  Register #(.trigger("falling"), .width(32)) register_2 (
    .D(data_out), .en(IR_enable), .clk(Clock), .Q({IR_31_27, IR_26_22, Immediate, OP}), .clr(hlt));
  RAM #(.addrWidth(6), .dataWidth(32)) ram_1 (
    .addr(multiplexer_1_out[5:0]), .we(write_enable), .oe(read_enable), .clk(Clock), .din(data_in),
    .dout(data_out));
  and and_1 (hlt, ~OP[0], ~OP[1], OP[2], OP[3]);  // AND_Gate

  assign IR_21_17 = Immediate[15:11];
endmodule

module Control_Unit (
  input  [5:0] OP,
  input  Clock,
  output RF_write,
  output C_select,
  output B_select,
  output [1:0] ALU_select,
  output move_select,
  output Z_select,
  output Y_select,
  output IR_enable,
  output PC_enable,
  output MA_select,
  output read_enable,
  output write_enable
);

  wire and_1_out, and_2_out, and_3_out, and_4_out, and_5_out, and_6_out, and_7_out, and_9_out, and_10_out,
       and_11_out, and_12_out, and_17_out, and_18_out, not_1_out, not_2_out, not_3_out, not_4_out, not_5_out,
       not_6_out, not_7_out, not_8_out;
  wire [2:0] counter_1_q;

  Counter #(.max('h4), .trigger("falling"), .width(3)) counter_1 (
    .Q(counter_1_q), .clk(Clock));  // open: load, D, count, carry, up, clr
  not not_1 (not_1_out, OP[3]);
  not not_2 (not_2_out, OP[2]);
  not not_3 (not_3_out, OP[1]);
  not not_4 (not_4_out, OP[0]);
  not not_5 (not_5_out, counter_1_q[2]);
  not not_6 (not_6_out, counter_1_q[1]);
  not not_7 (not_7_out, counter_1_q[0]);
  and and_1 (and_1_out, not_2_out, not_3_out, counter_1_q[2]);
  and and_2 (and_2_out, not_3_out, OP[0], counter_1_q[2]);
  and and_3 (and_3_out, OP[1], not_4_out, counter_1_q[2]);
  and and_4 (and_4_out, not_1_out, OP[2], counter_1_q[2]);
  and and_5 (and_5_out, OP[3], not_2_out, counter_1_q[2]);
  and and_6 (and_6_out, not_1_out, not_2_out);
  or or_1 (C_select, and_6_out, OP[0]);
  or or_2 (B_select, OP[0], and_7_out);
  and and_7 (and_7_out, not_1_out, not_2_out, OP[1]);
  and and_8 (ALU_select[1], OP[3], not_2_out);
  and and_9 (and_9_out, OP[2], OP[1]);
  or or_3 (ALU_select[0], and_9_out, and_10_out);
  and and_10 (and_10_out, OP[3], OP[1]);
  and and_11 (and_11_out, not_1_out, OP[2]);
  or or_4 (Z_select, OP[1], and_11_out, and_12_out);
  and and_12 (and_12_out, OP[3], not_2_out);
  and and_13 (Y_select, not_1_out, not_2_out, OP[1]);
  and and_14 (IR_enable, not_5_out, not_6_out, not_7_out);
  and and_15 (PC_enable, not_5_out, not_6_out, not_7_out);
  and and_16 (MA_select, not_5_out, not_6_out, not_7_out);
  and and_17 (and_17_out, not_5_out, not_6_out, not_7_out);
  or or_5 (read_enable, and_17_out, and_18_out);
  and and_18 (and_18_out, not_1_out, not_2_out, OP[1], not_4_out, counter_1_q[1], counter_1_q[0]);
  and and_19 (write_enable, not_1_out, not_2_out, OP[1], OP[0], counter_1_q[1], counter_1_q[0]);
  or or_6 (RF_write, and_1_out, and_2_out, and_3_out, and_4_out, and_5_out);
  not not_8 (not_8_out, Z_select);
  and and_20 (move_select, OP[0], not_8_out);
endmodule
